# Fritzing sketch testSetup (saved by Fritzing 0.9.3b)
stripboards: 3

parts:
  Raspberry_Pi_1 = Raspberry Pi 3 [part_number=RPI-3-V1.2]
  U1 = Module 4 Relais 5V [package="Module 4 Relais 5V"]
  DS1 = DS18B20 1-Wire Temperature Sensor Probe
  F1 = Fan - Ventilador [package=THT]
  Part1 = LCD1602-I2C
  M1 = Humidity and Temperature Sensor DHT11
  R1 = Resistor [tolerance=±5% resistance=1k package=THT]
  R2 = Resistor [tolerance=±5% resistance=1k package="0603 [SMD]"]

nets:
  3V3: Raspberry_Pi_1.3v3, DS1.VDD, R2.Pin_1
  N1: Raspberry_Pi_1.GPIO2, Part1.SDA
  N2: Raspberry_Pi_1.GPIO3, Part1.SCL
  N3: Raspberry_Pi_1.GIPO4, DS1.DQ, R2.Pin_0
  N4: Raspberry_Pi_1.GIPO11, M1.Data, R1.Pin_1
  GND: Raspberry_Pi_1.GND, U1.GND, DS1.GND, F1.GND, Part1.GND, M1.GND
  N5: Raspberry_Pi_1.GIPO8, U1.IN1
  N6: Raspberry_Pi_1.GIPO25, U1.IN2
  N7: Raspberry_Pi_1.GIPO24, U1.IN3
  N8: Raspberry_Pi_1.GIPO23, U1.IN4
  VCC: Raspberry_Pi_1.5V, U1.VCC, F1.5V, Part1.VCC, M1.Vcc, R1.Pin_0

notes:
  5V
  GND
  3V
  Humidifier
  Fan
  Heating mat

custom parts:
  Module 4 Relais 5V: Module 4 Relais 5V 4x SPD-06VDC-SD-C
  Fan - Ventilador: Ventilador de 2 pines, se encuentra comunmente en computadoras de escritorio
  LCD1602-I2C: A standard character display, usually with 2x16 characters. Comes in many colors with LCM1602 IIC attached.
  Humidity and Temperature Sensor DHT11: Digital relative humidity & temperature sensor DHT11
